// Logisim project Basic-gates..circ as structural Verilog: 1 circuit, main circuit main
module main (
  input  in_1,
  input  in_2,
  input  in_3,
  input  in_4,
  input  in_5,
  input  in_6,
  input  in_7,
  input  in_8,
  input  in_9,
  input  in_10,
  input  in_11,
  output out_12,
  output out_13
);

  wire and_1_out, and_2_out, and_3_out, and_4_out, not_1_out, not_2_out, not_3_out, not_5_out, or_1_out,
       or_2_out;

  not not_1 (not_1_out, in_11);
  not not_2 (not_2_out, in_10);
  and and_1 (and_1_out, in_1, in_2);
  or or_1 (or_1_out, in_3, in_4);
  not not_3 (not_3_out, in_5);
  LED led_1 (.in(not_3_out));
  and and_2 (and_2_out, in_6, in_7);
  or or_2 (or_2_out, in_8, in_9);
  LED led_2 (.in(and_1_out));
  LED led_3 (.in(or_1_out));
  not not_4 (out_12, or_2_out);
  and and_3 (and_3_out, in_10, not_1_out);
  and and_4 (and_4_out, not_2_out, in_11);
  not not_5 (not_5_out, and_2_out);
  LED led_4 (.in(not_5_out));
  or or_3 (out_13, and_3_out, and_4_out);
endmodule
